// Logisim project 1220649_1220775_1220523.circ as structural Verilog: 4 circuits, main circuit RFile
module ALU (
  input  [31:0] A,
  input  [31:0] B,
  input  [3:0] ALU_OPRATION,
  output [31:0] ALU_Result
);

  wire comparator_1_eq, comparator_2_lt;
  wire [31:0] Add, AND, CAND, NADD, not_1_out, OR, ROR, SEQ, SLL, SLT, SRA, SRL, XOR;

  assign not_1_out = ~A;  // NOT_Gate not_1, 32 bits wide
  assign AND = A & B;  // AND_Gate and_1, 32 bits wide
  assign OR = A | B;  // OR_Gate or_1, 32 bits wide
  assign CAND = not_1_out & B;  // AND_Gate and_2, 32 bits wide
  Adder #(.width(32)) adder_1 (.a(A), .b(B), .out(Add));  // open: cin, cout
  Comparator #(.width(32)) comparator_1 (.a(A), .b(B), .eq(comparator_1_eq));  // open: gt, lt
  Comparator #(.width(32)) comparator_2 (.a(A), .b(B), .lt(comparator_2_lt));  // open: gt, eq
  Shifter #(.width(32), .shift("ar")) shifter_1 (.in(A), .\dist (B[4:0]), .out(SRA));
  Shifter #(.width(32)) shifter_2 (.in(A), .\dist (B[4:0]), .out(SLL));
  Shifter #(.width(32), .shift("lr")) shifter_3 (.in(A), .\dist (B[4:0]), .out(SRL));
  Shifter #(.width(32), .shift("rr")) shifter_4 (.in(A), .\dist (B[4:0]), .out(ROR));
  Subtractor #(.width(32)) subtractor_1 (.a(B), .b(A), .out(NADD));  // open: bin, bout
  assign XOR = A ^ B;  // XOR_Gate xor_1, 32 bits wide
  assign SEQ = {{31{1'b0}}, comparator_1_eq};  // Bit_Extender bit_extender_1
  assign SLT = {{31{1'b0}}, comparator_2_lt};  // Bit_Extender bit_extender_2
  Multiplexer #(.select(4), .width(32), .enable("false")) multiplexer_1 (
    .in0(XOR), .in1(AND), .in2(OR), .in3(CAND), .in4(Add), .in5(SEQ), .in6(NADD), .in7(SLT), .in8(SRA),
    .in9(SRL), .in10(SLL), .in11(ROR), .out(ALU_Result), .sel(ALU_OPRATION));  // open: in12, in13, in14, in15
endmodule

module RFile (
  input  [2:0] RZ,
  input  [2:0] Ry,
  input  [31:0] Bus_X,
  input  [2:0] Rx,
  input  Reg_Write,
  input  CLK,
  output [31:0] BusY,
  output [31:0] BusZ
);

  wire and1_out, and2_out, and_3_out, and_4_out, and_5_out, and_6_out, and_7_out, decoder_1_out0,
       decoder_2_out0, decoder_2_out1, decoder_2_out2, decoder_2_out3, decoder_2_out4, decoder_2_out5,
       decoder_2_out6, decoder_2_out7, decoder_3_out0, decoder_3_out1, decoder_3_out2, decoder_3_out3,
       decoder_3_out4, decoder_3_out5, decoder_3_out6, decoder_3_out7, R1, R2, R3, R4, R5, R6, R7;
  wire [31:0] Reg_1_q, Reg_2_q, Reg_3_q, Reg_4_q, Reg_5_q, Reg_6_q, Reg_7_q;

  Decoder #(.select(3), .enable("false")) decoder_1 (
    .out0(decoder_1_out0), .out1(R1), .out2(R2), .out3(R3), .out4(R4), .out5(R5), .out6(R6), .out7(R7),
    .sel(Rx));
  and and1 (and1_out, R1, Reg_Write);
  and and2 (and2_out, R2, Reg_Write);
  and and_3 (and_3_out, R3, Reg_Write);
  and and_4 (and_4_out, R4, Reg_Write);
  and and_5 (and_5_out, R5, Reg_Write);
  and and_6 (and_6_out, R6, Reg_Write);
  and and_7 (and_7_out, R7, Reg_Write);
  Register #(.width(32)) Reg_1 (.D(Bus_X), .en(and1_out), .Q(Reg_1_q), .clk(CLK));  // open: clr
  Register #(.width(32)) Reg_2 (.D(Bus_X), .en(and2_out), .Q(Reg_2_q), .clk(CLK));  // open: clr
  Register #(.width(32)) Reg_3 (.D(Bus_X), .en(and_3_out), .Q(Reg_3_q), .clk(CLK));  // open: clr
  Register #(.width(32)) Reg_4 (.D(Bus_X), .en(and_4_out), .Q(Reg_4_q), .clk(CLK));  // open: clr
  Register #(.width(32)) Reg_5 (.D(Bus_X), .en(and_5_out), .Q(Reg_5_q), .clk(CLK));  // open: clr
  Register #(.width(32)) Reg_6 (.D(Bus_X), .en(and_6_out), .Q(Reg_6_q), .clk(CLK));  // open: clr
  Register #(.width(32)) Reg_7 (.D(Bus_X), .en(and_7_out), .Q(Reg_7_q), .clk(CLK));  // open: clr
  assign BusY = decoder_2_out0 ? {32{1'b0}} : 32'bz;  // Controlled_Buffer controlled_buffer_1
  assign BusY = decoder_2_out1 ? Reg_1_q : 32'bz;  // Controlled_Buffer controlled_buffer_2
  assign BusY = decoder_2_out2 ? Reg_2_q : 32'bz;  // Controlled_Buffer controlled_buffer_3
  assign BusY = decoder_2_out3 ? Reg_3_q : 32'bz;  // Controlled_Buffer controlled_buffer_4
  assign BusY = decoder_2_out4 ? Reg_4_q : 32'bz;  // Controlled_Buffer controlled_buffer_5
  assign BusY = decoder_2_out5 ? Reg_5_q : 32'bz;  // Controlled_Buffer controlled_buffer_6
  assign BusY = decoder_2_out6 ? Reg_6_q : 32'bz;  // Controlled_Buffer controlled_buffer_7
  assign BusY = decoder_2_out7 ? Reg_7_q : 32'bz;  // Controlled_Buffer controlled_buffer_8
  Decoder #(.select(3), .enable("false")) decoder_2 (
    .out0(decoder_2_out0), .out1(decoder_2_out1), .out2(decoder_2_out2), .out3(decoder_2_out3),
    .out4(decoder_2_out4), .out5(decoder_2_out5), .out6(decoder_2_out6), .out7(decoder_2_out7), .sel(Ry));
  assign BusZ = decoder_3_out0 ? {32{1'b0}} : 32'bz;  // Controlled_Buffer controlled_buffer_9
  assign BusZ = decoder_3_out1 ? Reg_1_q : 32'bz;  // Controlled_Buffer controlled_buffer_10
  assign BusZ = decoder_3_out2 ? Reg_2_q : 32'bz;  // Controlled_Buffer controlled_buffer_11
  assign BusZ = decoder_3_out3 ? Reg_3_q : 32'bz;  // Controlled_Buffer controlled_buffer_12
  assign BusZ = decoder_3_out4 ? Reg_4_q : 32'bz;  // Controlled_Buffer controlled_buffer_13
  assign BusZ = decoder_3_out5 ? Reg_5_q : 32'bz;  // Controlled_Buffer controlled_buffer_14
  assign BusZ = decoder_3_out6 ? Reg_6_q : 32'bz;  // Controlled_Buffer controlled_buffer_15
  assign BusZ = decoder_3_out7 ? Reg_7_q : 32'bz;  // Controlled_Buffer controlled_buffer_16
  Decoder #(.select(3), .enable("false")) decoder_3 (
    .out0(decoder_3_out0), .out1(decoder_3_out1), .out2(decoder_3_out2), .out3(decoder_3_out3),
    .out4(decoder_3_out4), .out5(decoder_3_out5), .out6(decoder_3_out6), .out7(decoder_3_out7), .sel(RZ));

  // Other names for the same wires on the sheet: BusX[31:0] = Bus_X
endmodule

module Datapath (
  input  [4:0] OpCode,
  input  [1:0] f,
  output [1:0] Data_from_here,
  output dis_address,
  output memoread,
  output signed_or_not,
  output memowrite,
  output write_control_in_register,
  output [1:0] zreg_or_imm5,
  output [3:0] ALU_OPRATION,
  output [2:0] jump_or_add_2
);

  wire clock, comparator_1_eq, comparator_2_eq, comparator_3_lt, comparator_4_lt, not_1_out, not_2_out;
  wire [1:0] F_t;
  wire [2:0] LMM3, multiplexer_7_out;
  wire [3:0] ALUop;
  wire [4:0] OP, shifter_1_out;
  wire [4:2] LMM5;
  wire [7:5] LMM11;
  wire [10:0] shifter_2_out, shifter_3_out;
  wire [19:0] bit_extender_1_out, bit_extender_5_out, curr_pc, jump_R_IMM5, jump_R_imm11, multiplexer_1_out,
       multiplexer_2_out, multiplexer_3_out, multiplexer_4_out, multiplexer_5_out, pc_2;
  wire [31:0] alu_1_alu_result, bit_extender_2_out, bit_extender_3_out, bit_extender_4_out,
       bit_extender_6_out, bit_extender_7_out, multiplexer_8_out, new_LMM5, ram_1_data, result, rfile_1_busy,
       rfile_1_busz;

  ROM #(.addrWidth(5), .dataWidth(9)) rom_1 (
    .addr(OP),
    .data({dis_address, write_control_in_register, signed_or_not, zreg_or_imm5, memowrite, memoread, Data_from_here}));  // open: sel
  ROM #(.addrWidth(5), .dataWidth(3)) rom_2 (.addr(OP), .data(jump_or_add_2));  // open: sel
  ROM #(.addrWidth(7), .dataWidth(4)) rom_3 (.addr({OP, f}), .data(ALUop));  // open: sel
  Comparator #(.width(3)) comparator_1 (.a(LMM3), .b(LMM11), .eq(comparator_1_eq));  // open: gt, lt
  Comparator #(.width(3)) comparator_2 (.a(LMM3), .b(LMM11), .eq(comparator_2_eq));  // open: gt, lt
  Multiplexer #(.width(20), .enable("false")) multiplexer_1 (
    .in0(pc_2), .in1(jump_R_IMM5), .out(multiplexer_1_out), .sel(comparator_1_eq));
  Multiplexer #(.width(20), .enable("false")) multiplexer_2 (
    .in0(pc_2), .in1(jump_R_IMM5), .out(multiplexer_2_out), .sel(not_1_out));
  not not_1 (not_1_out, comparator_2_eq);
  Comparator #(.width(3)) comparator_3 (.a(LMM3), .b(LMM11), .lt(comparator_3_lt));  // open: gt, eq
  Shifter #(.width(5)) shifter_1 (.in({LMM5, F_t}), .\dist (3'b001), .out(shifter_1_out));
  Multiplexer #(.width(20), .enable("false")) multiplexer_3 (
    .in0(pc_2), .in1(jump_R_IMM5), .out(multiplexer_3_out), .sel(comparator_3_lt));
  Comparator #(.width(3)) comparator_4 (.a(LMM3), .b(LMM11), .lt(comparator_4_lt));  // open: gt, eq
  not not_2 (not_2_out, comparator_4_lt);
  assign bit_extender_1_out = {{15{shifter_1_out[4]}}, shifter_1_out};  // Bit_Extender bit_extender_1
  Multiplexer #(.width(20), .enable("false")) multiplexer_4 (
    .in0(pc_2), .in1(jump_R_IMM5), .out(multiplexer_4_out), .sel(not_2_out));
  Multiplexer #(.select(3), .width(20), .enable("false")) multiplexer_5 (
    .in0(pc_2), .in1(multiplexer_1_out), .in2(multiplexer_2_out), .in3(multiplexer_3_out),
    .in4(multiplexer_4_out), .in5(jump_R_imm11), .in6({20{1'b0}}), .out(multiplexer_5_out),
    .sel(jump_or_add_2));  // open: in7
  Clock clock_1 (.out(clock));
  Adder #(.width(20)) adder_1 (.a(bit_extender_1_out), .b(curr_pc), .out(jump_R_IMM5));  // open: cin, cout
  Register #(.width(20)) PC (.D(multiplexer_5_out), .en(1'b1), .Q(curr_pc), .clk(clock));  // open: clr
  Adder #(.width(20)) adder_2 (.a(curr_pc), .b(20'h2), .out(pc_2));  // open: cin, cout
  assign bit_extender_2_out = {{27{1'b0}}, {LMM5, F_t}};  // Bit_Extender bit_extender_2
  assign bit_extender_3_out = {{27{LMM5[4]}}, {LMM5, F_t}};  // Bit_Extender bit_extender_3
  ROM #(.addrWidth(20), .dataWidth(16)) rom_4 (.addr(curr_pc), .data({OP, LMM3, LMM11, LMM5, F_t}));  // open: sel
  Multiplexer #(.width(32), .enable("false")) multiplexer_6 (
    .in0(bit_extender_2_out), .in1(bit_extender_3_out), .out(new_LMM5), .sel(signed_or_not));
  Multiplexer #(.width(3), .enable("false")) multiplexer_7 (
    .in0(LMM3), .in1(3'b111), .out(multiplexer_7_out), .sel(dis_address));
  RFile rfile_1 (
    .RZ(LMM5), .Ry(LMM11), .Bus_X(result), .Rx(multiplexer_7_out), .BusY(rfile_1_busy), .BusZ(rfile_1_busz),
    .Reg_Write(write_control_in_register), .CLK(clock));
  Multiplexer #(.select(2), .width(32), .enable("false")) multiplexer_8 (
    .in0(rfile_1_busz), .in1(new_LMM5), .in2(bit_extender_4_out), .in3(bit_extender_6_out),
    .out(multiplexer_8_out), .sel(zreg_or_imm5));
  assign bit_extender_4_out = {{27{LMM3[2]}}, {LMM3, F_t}};  // Bit_Extender bit_extender_4
  Shifter #(.width(11)) shifter_2 (.in({LMM3, LMM11, LMM5, F_t}), .\dist (4'b0001), .out(shifter_2_out));
  ALU alu_1 (.A(rfile_1_busy), .B(multiplexer_8_out), .ALU_OPRATION(ALUop), .ALU_Result(alu_1_alu_result));
  assign bit_extender_5_out = {{9{shifter_2_out[10]}}, shifter_2_out};  // Bit_Extender bit_extender_5
  Shifter #(.width(11)) shifter_3 (.in({LMM3, LMM11, LMM5, F_t}), .\dist (4'b0001), .out(shifter_3_out));
  Adder #(.width(20)) adder_3 (.a(bit_extender_5_out), .b(curr_pc), .out(jump_R_imm11));  // open: cin, cout
  assign bit_extender_6_out = {{21{shifter_3_out[10]}}, shifter_3_out};  // Bit_Extender bit_extender_6
  RAM #(.addrWidth(20), .dataWidth(32), .bus("separate")) ram_1 (
    .addr(alu_1_alu_result[19:0]), .din(rfile_1_busz), .data(ram_1_data), .str(memowrite), .clk(clock),
    .ld(memoread));  // open: sel, clr
  assign bit_extender_7_out = {{12{pc_2[19]}}, pc_2};  // Bit_Extender bit_extender_7
  Multiplexer #(.select(2), .width(32), .enable("false")) multiplexer_9 (
    .in0(alu_1_alu_result), .in1(ram_1_data), .in2(bit_extender_7_out), .out(result), .sel(Data_from_here));  // open: in3

  // Other names for the same wires on the sheet: Data_from_where[1:0] = Data_from_here;
  //   LMM11 (some bits) = {LMM3, LMM5, F_t}; Z[2:0] = LMM5; Y[2:0] = LMM11; LMM2[1:0] = F_t; LMM5[1:0] = F_t;
  //   X[2:0] = LMM3

  // Notes on the sheet:
  //   contents of rom_1 (hex, n*v repeats v):
  //   82 82 4*92 5*d2 92 92 92 4*0 d5 28 0 180
  //   contents of rom_2 (hex, n*v repeats v):
  //   15*0 1 2 3 4 5 6
  //   contents of rom_3 (hex, n*v repeats v):
  //   1 3 2 0 4 6 5 7 4*1 4*3 4*2 4*0 4*4 4*6 4*5 4*7 4*a 4*9 4*8 4*b
  //                                   instruction memory
  //   contents of rom_4 (hex, n*v repeats v):
  //   668 0 670 0 671 0 672 0 673 0 d70 0 d71 0 d72 0 d73 0 1221 0 7221 0 7 0 a21 0 8221 0 8a21 0 9221 0
  //   9a21 0 a221 0 aa21
endmodule

module ControlUnit (
  input  [4:0] OpCode,
  input  [1:0] f,
  output [1:0] Data_from_here,
  output dis_address,
  output memoread,
  output signed_or_not,
  output memowrite,
  output write_control_in_register,
  output [1:0] zreg_or_imm5,
  output [3:0] ALU_OPRATION,
  output [1:0] jump_or_add_2
);

  ROM #(.addrWidth(5), .dataWidth(9)) rom_1 (
    .addr(OpCode),
    .data({dis_address, write_control_in_register, signed_or_not, zreg_or_imm5, memowrite, memoread, Data_from_here}));  // open: sel
  ROM #(.addrWidth(5), .dataWidth(2)) rom_2 (.addr(OpCode), .data(jump_or_add_2));  // open: sel
  ROM #(.addrWidth(7), .dataWidth(4)) rom_3 (.addr({OpCode, f}), .data(ALU_OPRATION));  // open: sel

  // Notes on the sheet:
  //   contents of rom_1 (hex, n*v repeats v):
  //   82 82 4*92 5*d2 92 92 92 4*0 d5 28 0 180
  //   contents of rom_2 (hex, n*v repeats v):
  //   14*0 3 0 1 2 0 0 2 2
  //   contents of rom_3 (hex, n*v repeats v):
  //   1 3 2 0 4 6 5 7 4*1 4*3 4*2 4*0 4*4 4*6 4*5 4*7 4*a 4*9 4*8 4*b
endmodule
